# Fritzing sketch toggle_button_debounce (saved by Fritzing 1.0.1rc)
breadboards: 1

parts:
  A1 = Arduino UNO R4 WiFi
  LED1 = smd LED [color="Red (633nm)" package="0603 [SMD]"]
  S1 = Pushbutton [package="[THT]"]
  R1 = Resistor [tolerance=±5% resistance=220 package="0402 [SMD]"]
  R2 = Resistor [tolerance=±5% resistance=220 package="0402 [SMD]"]

nets:
  N1: A1.Pin_2, A1.Pin_10, A1.Pin_30, A1.Pin_48, LED1.cathode, R2.Pin_0
  N2: A1.Pin_8, S1.Pin_1, S1.Pin_2
  N3: A1.Pin_36, S1.Pin_3, S1.Pin_4, R2.Pin_1
  N4: A1.Pin_47, R1.Pin_1
  N5: LED1.anode, R1.Pin_0

custom parts:
  Arduino UNO R4 WiFi: The Arduino UNO R4 WiFi merges the RA4M1 microprocessor from Renesas with the ESP32-S3 from Espressif, creating an all-in-one tool for makers with enhanced processing power and a diverse array of new peripherals.
